// Logisim project Lab1_TOP_B_Clement Samuel Marly_2206082114.circ as structural Verilog: 7 circuits, main circuit 1ai
module _1ai (
  input  A,
  input  B,
  input  D,
  output F
);

  wire not_1_out, not_2_out;

  not not_1 (not_1_out, B);
  not not_2 (not_2_out, D);
  or or_1 (F, A, not_1_out, not_2_out);
endmodule

module _1aii (
  input  A,
  input  B,
  input  C,
  output F
);

  wire not_1_out, not_2_out, not_3_out, not_4_out, not_5_out, not_6_out, or_1_out, or_2_out, or_3_out,
       or_4_out;

  not not_1 (not_1_out, B);
  not not_2 (not_2_out, B);
  not not_3 (not_3_out, C);
  not not_4 (not_4_out, A);
  not not_5 (not_5_out, B);
  not not_6 (not_6_out, C);
  or or_1 (or_1_out, A, B, C);
  or or_2 (or_2_out, A, not_1_out, C);
  or or_3 (or_3_out, A, not_2_out, not_3_out);
  or or_4 (or_4_out, not_4_out, not_5_out, not_6_out);
  and and_1 (F, or_1_out, or_2_out, or_3_out, or_4_out);
endmodule

module _1aiii (
  input  A,
  input  B,
  input  C,
  input  D,
  output F
);

  wire not_1_out, not_2_out, not_3_out, not_4_out, or_1_out, or_2_out, or_3_out;

  not not_1 (not_1_out, D);
  not not_2 (not_2_out, B);
  not not_3 (not_3_out, C);
  not not_4 (not_4_out, A);
  or or_1 (or_1_out, A, C, not_1_out);
  and and_1 (F, or_1_out, or_2_out, or_3_out);
  or or_2 (or_2_out, not_2_out, not_3_out);
  or or_3 (or_3_out, not_4_out, B, C, D);
endmodule

module _1bi (
  input  A,
  input  B,
  input  C,
  input  D,
  output F
);

  wire nand_1_out, nand_2_out, nand_3_out, nand_4_out, nand_5_out, nand_6_out, nand_7_out;

  nand nand_1 (nand_1_out, A, A);
  nand nand_2 (nand_2_out, B, B);
  nand nand_3 (nand_3_out, C, C);
  nand nand_4 (nand_4_out, nand_1_out, B, C, D);
  nand nand_5 (nand_5_out, A, nand_2_out, C, D);
  nand nand_6 (nand_6_out, A, B, nand_3_out, D);
  nand nand_7 (nand_7_out, A, B, C, D);
  nand nand_8 (F, nand_4_out, nand_5_out, nand_6_out, nand_7_out);
endmodule

module _1bii (
  input  A,
  input  B,
  input  C,
  input  D,
  output F
);

  wire nor_1_out, nor_2_out, nor_3_out, nor_4_out, nor_5_out, nor_6_out, nor_7_out, nor_8_out, nor_9_out,
       nor_10_out, nor_11_out, nor_12_out, nor_13_out, nor_14_out, nor_15_out, nor_16_out;

  nor nor_1 (nor_1_out, A, A);
  nor nor_2 (nor_2_out, B, B);
  nor nor_3 (nor_3_out, D, D);
  nor nor_4 (nor_4_out, nor_1_out, C);
  nor nor_5 (nor_5_out, B, nor_3_out);
  nor nor_6 (nor_6_out, nor_2_out, D);
  nor nor_7 (nor_7_out, nor_8_out, nor_8_out);
  nor nor_8 (nor_8_out, nor_4_out, nor_4_out);
  nor nor_9 (nor_9_out, nor_5_out, nor_5_out);
  nor nor_10 (nor_10_out, A, nor_11_out);
  nor nor_11 (nor_11_out, nor_6_out, nor_6_out);
  nor nor_12 (nor_12_out, nor_7_out, nor_13_out);
  nor nor_13 (nor_13_out, nor_9_out, nor_9_out);
  nor nor_14 (nor_14_out, nor_10_out, nor_10_out);
  nor nor_15 (nor_15_out, nor_12_out, nor_12_out);
  nor nor_16 (nor_16_out, nor_14_out, nor_14_out);
  nor nor_17 (F, nor_15_out, nor_16_out);
endmodule

module _1biii (
  input  W,
  input  X,
  input  Y,
  input  Z,
  output F
);

  wire nand_1_out, nand_2_out, nand_3_out, nand_4_out, nand_5_out, nand_6_out, nand_7_out, nand_8_out;

  nand nand_1 (nand_1_out, Y, Y);
  nand nand_2 (nand_2_out, W, W);
  nand nand_3 (nand_3_out, X, X);
  nand nand_4 (nand_4_out, Z, Z);
  nand nand_5 (nand_5_out, Y, Y);
  nand nand_6 (nand_6_out, W, nand_1_out, Z);
  nand nand_7 (nand_7_out, nand_2_out, nand_3_out, nand_4_out);
  nand nand_8 (nand_8_out, X, nand_5_out);
  nand nand_9 (F, nand_6_out, nand_7_out, nand_8_out);
endmodule

module _2b (
  input  A,
  input  B,
  input  C,
  input  D,
  output A2,
  output B2,
  output C2
);

  wire and_1_out, and_2_out, and_3_out, and_4_out, and_5_out, and_6_out, and_7_out, and_8_out, and_9_out,
       and_10_out, and_11_out, and_12_out, and_13_out, and_14_out, and_15_out, and_16_out, and_17_out,
       and_18_out, not_1_out, not_2_out, not_3_out, not_4_out, not_5_out, not_6_out, not_7_out, not_8_out,
       not_9_out, not_10_out, not_11_out, not_12_out, not_13_out, not_14_out, not_15_out, not_16_out,
       not_17_out, not_18_out, not_19_out, not_20_out, not_21_out, not_22_out, not_23_out, not_24_out,
       not_25_out, not_26_out, not_27_out, not_28_out, not_29_out, not_30_out, not_31_out, not_32_out,
       not_33_out, not_34_out, not_35_out, not_36_out, not_37_out, not_38_out;

  not not_1 (not_1_out, A);
  not not_2 (not_2_out, B);
  not not_3 (not_3_out, D);
  not not_4 (not_4_out, A);
  not not_5 (not_5_out, C);
  not not_6 (not_6_out, D);
  not not_7 (not_7_out, A);
  not not_8 (not_8_out, B);
  not not_9 (not_9_out, C);
  not not_10 (not_10_out, D);
  not not_11 (not_11_out, B);
  not not_12 (not_12_out, D);
  not not_13 (not_13_out, C);
  not not_14 (not_14_out, D);
  not not_15 (not_15_out, A);
  not not_16 (not_16_out, B);
  not not_17 (not_17_out, D);
  not not_18 (not_18_out, A);
  not not_19 (not_19_out, B);
  not not_20 (not_20_out, D);
  not not_21 (not_21_out, A);
  not not_22 (not_22_out, C);
  not not_23 (not_23_out, B);
  not not_24 (not_24_out, C);
  not not_25 (not_25_out, B);
  not not_26 (not_26_out, C);
  not not_27 (not_27_out, D);
  not not_28 (not_28_out, A);
  not not_29 (not_29_out, B);
  not not_30 (not_30_out, C);
  not not_31 (not_31_out, D);
  not not_32 (not_32_out, A);
  not not_33 (not_33_out, B);
  not not_34 (not_34_out, C);
  not not_35 (not_35_out, A);
  not not_36 (not_36_out, B);
  not not_37 (not_37_out, A);
  not not_38 (not_38_out, D);
  and and_1 (and_1_out, not_1_out, not_2_out, C, not_3_out);
  and and_2 (and_2_out, not_4_out, B, not_5_out, not_6_out);
  and and_3 (and_3_out, not_7_out, B, C, D);
  and and_4 (and_4_out, A, not_8_out, not_9_out, not_10_out);
  and and_5 (and_5_out, A, not_11_out, C, not_12_out);
  and and_6 (and_6_out, A, B, not_13_out, not_14_out);
  and and_7 (and_7_out, not_15_out, not_16_out, C, not_17_out);
  and and_8 (and_8_out, not_18_out, not_19_out, C, not_20_out);
  and and_9 (and_9_out, not_21_out, B, not_22_out, D);
  and and_10 (and_10_out, A, not_23_out, not_24_out, D);
  and and_11 (and_11_out, A, not_25_out, C, D);
  and and_12 (and_12_out, A, B, not_26_out, D);
  and and_13 (and_13_out, A, B, C, not_27_out);
  and and_14 (and_14_out, not_28_out, not_29_out, not_30_out, not_31_out);
  and and_15 (and_15_out, not_32_out, not_33_out, not_34_out, D);
  and and_16 (and_16_out, not_35_out, not_36_out, C, D);
  and and_17 (and_17_out, not_37_out, B, C, not_38_out);
  and and_18 (and_18_out, A, B, C, D);
  or or_1 (A2, and_1_out, and_2_out, and_3_out, and_4_out, and_5_out, and_6_out, and_7_out, and_8_out);
  or or_2 (B2, and_9_out, and_10_out, and_11_out, and_12_out, and_13_out);
  or or_3 (C2, and_14_out, and_15_out, and_16_out, and_17_out, and_18_out);
endmodule
