// Logisim project Lab2_TOP_B_ClementSamuelMarly_2206082114.circ as structural Verilog: 12 circuits, main circuit 1.c
module _1_c (
  input  A,
  input  B,
  input  C,
  input  D,
  output Geprek_bansai,
  output Susi_hero,
  output Kaeftji
);

  wire and_1_out, and_2_out, and_3_out, and_4_out, and_5_out, and_6_out, not_1_out, not_2_out, not_3_out,
       not_4_out, not_5_out, not_6_out, not_7_out, not_8_out, not_9_out;

  not not_1 (not_1_out, A);
  and and_1 (and_1_out, not_1_out, D);
  not not_2 (not_2_out, C);
  and and_2 (and_2_out, not_2_out, D);
  and and_3 (and_3_out, B, D);
  not not_3 (not_3_out, A);
  not not_4 (not_4_out, B);
  and and_4 (and_4_out, not_3_out, not_4_out, C);
  not not_5 (not_5_out, A);
  not not_6 (not_6_out, C);
  not not_7 (not_7_out, D);
  not not_8 (not_8_out, B);
  not not_9 (not_9_out, D);
  or or_1 (Geprek_bansai, and_1_out, and_2_out);
  or or_2 (Susi_hero, and_3_out, and_4_out);
  and and_5 (and_5_out, not_5_out, B, not_6_out, not_7_out);
  or or_3 (Kaeftji, and_5_out, and_6_out);
  and and_6 (and_6_out, not_8_out, C, not_9_out);

  // Notes on the sheet:
  //   Circuit ini dibuat dari K-maps dengan memasukkan don't care karena dianggap input tidak mungkin sampai angka lebih dari 12
endmodule

module _1_d (
  input  A,
  input  B,
  input  C,
  input  D,
  output Geprek_bansai,
  output Susi_hero,
  output Kaeftji
);

  wire and_1_out, and_2_out, and_3_out, and_4_out, and_5_out, and_6_out, not_1_out, not_2_out, not_3_out,
       not_4_out, not_5_out, not_6_out, not_7_out, not_8_out, not_9_out, not_10_out, not_11_out;

  not not_1 (not_1_out, A);
  and and_1 (and_1_out, not_1_out, D);
  not not_2 (not_2_out, B);
  and and_2 (and_2_out, not_2_out, not_3_out, D);
  not not_3 (not_3_out, C);
  not not_4 (not_4_out, A);
  not not_5 (not_5_out, B);
  and and_3 (and_3_out, not_4_out, not_5_out, C);
  not not_6 (not_6_out, A);
  and and_4 (and_4_out, not_6_out, B, D);
  not not_7 (not_7_out, B);
  not not_8 (not_8_out, D);
  not not_9 (not_9_out, A);
  not not_10 (not_10_out, C);
  not not_11 (not_11_out, D);
  or or_1 (Geprek_bansai, and_1_out, and_2_out);
  or or_2 (Susi_hero, and_3_out, and_4_out);
  and and_5 (and_5_out, not_7_out, C, not_8_out);
  or or_3 (Kaeftji, and_5_out, and_6_out);
  and and_6 (and_6_out, not_9_out, B, not_10_out, not_11_out);

  // Notes on the sheet:
  //   Circuit ini dibuat dengan mengeluarkan don't care karena dianggap input angka hanya sampai 12
endmodule

module _2_tipe_1 (
  input  Halte_Lenteng_Lantung,
  input  [1:0] Halte_Pondok_Jepang,
  input  placeholder,
  output _0,
  output _1,
  output _2,
  output _3,
  output _4,
  output _5,
  output _6,
  output _7,
  output _8,
  output _9,
  output _10,
  output _11,
  output _12,
  output _13,
  output _14,
  output _15,
  output Bis_Berangkat
);

  wire [3:0] full_adder_1_c, halte_lenteng_lantung_1_a, halte_pondok_jepang_1_a_2;

  Halte_Lenteng_Lantung halte_lenteng_lantung_1 (.in_1(Halte_Lenteng_Lantung), .A(halte_lenteng_lantung_1_a));
  Halte_Pondok_Jepang halte_pondok_jepang_1 (.A(Halte_Pondok_Jepang), .A_2(halte_pondok_jepang_1_a_2));
  Full_adder full_adder_1 (
    .A(halte_lenteng_lantung_1_a), .B(halte_pondok_jepang_1_a_2), .C0(placeholder),
    .C({Bis_Berangkat, full_adder_1_c}));  // open: out_4
  binary_converter_4_bit binary_converter_4_bit_1 (
    .Jumlah_penumpang(full_adder_1_c), .out_2(_0), .out_3(_1), .out_4(_2), .out_5(_3), .out_6(_4),
    .out_7(_5), .out_8(_6), .out_9(_7), .out_10(_8), .out_11(_9), .out_12(_10), .out_13(_11), .out_14(_12),
    .out_15(_13), .out_16(_14), .out_17(_15));

  // Notes on the sheet:
  //   Dianggap penumpang bus akan selalu maksimum
  //   0 = 14
  //   1 = 7
  //   0 = 10
  //   1 = 4
  //   2 = 6
  //   3 = 9
  //   Jumlah penumpang menunggu
endmodule

module _2_tipe_2 (
  input  Selector_Halte_Lenteng_Lantung,
  input  [3:0] Jalur_0,
  input  [3:0] Jalur_1,
  input  [1:0] Selector_Halte_Pondok_Jepang,
  input  [3:0] Jalur_0_2,
  input  [3:0] Jalur_1_2,
  input  Placeholder,
  input  [3:0] Jalur_2,
  input  [3:0] Jalur_3,
  output _0,
  output _1,
  output _2,
  output _3,
  output _4,
  output _5,
  output _6,
  output _7,
  output _8,
  output _9,
  output _10,
  output _11,
  output _12,
  output _13,
  output _14,
  output _15,
  output Bis_Berangkat
);

  wire [3:0] full_adder_1_c, multiplexer_lenteng_lantung_1_penumpang_halte_lenteng_lantung,
       multiplexer_pondok_jepang_1_penumpang_halte_pondok_jepang;

  Multiplexer_Lenteng_Lantung multiplexer_lenteng_lantung_1 (
    .in_1(Selector_Halte_Lenteng_Lantung), .Jalur_0(Jalur_0), .Jalur_1(Jalur_1),
    .Penumpang_halte_Lenteng_Lantung(multiplexer_lenteng_lantung_1_penumpang_halte_lenteng_lantung));
  Multiplexer_Pondok_Jepang multiplexer_pondok_jepang_1 (
    .in_1(Selector_Halte_Pondok_Jepang[1]), .in_2(Selector_Halte_Pondok_Jepang[0]), .Jalur_0(Jalur_0_2),
    .Jalur_1(Jalur_1_2), .Jalur_2(Jalur_2), .Jalur_3(Jalur_3),
    .Penumpang_halte_Pondok_Jepang(multiplexer_pondok_jepang_1_penumpang_halte_pondok_jepang));
  Full_adder full_adder_1 (
    .A(multiplexer_lenteng_lantung_1_penumpang_halte_lenteng_lantung),
    .B(multiplexer_pondok_jepang_1_penumpang_halte_pondok_jepang), .C0(Placeholder),
    .C({Bis_Berangkat, full_adder_1_c}));  // open: out_4
  binary_converter_4_bit binary_converter_4_bit_1 (
    .Jumlah_penumpang(full_adder_1_c), .out_2(_0), .out_3(_1), .out_4(_2), .out_5(_3), .out_6(_4),
    .out_7(_5), .out_8(_6), .out_9(_7), .out_10(_8), .out_11(_9), .out_12(_10), .out_13(_11), .out_14(_12),
    .out_15(_13), .out_16(_14), .out_17(_15));

  // Notes on the sheet:
  //   Penumpang bus dianggap masukkan dari input petugas
  //   Jumlah penumpang menunggu
endmodule

module adder (
  input  in_1,
  input  in_2,
  input  in_3,
  output S,
  output C
);

  wire and_1_out, and_2_out, xor_1_out;

  xor xor_1 (xor_1_out, in_1, in_2);
  xor xor_2 (S, xor_1_out, in_3);
  and and_1 (and_1_out, xor_1_out, in_3);
  and and_2 (and_2_out, in_1, in_2);
  or or_1 (C, and_1_out, and_2_out);
endmodule

module Full_adder (
  input  [3:0] A,
  input  [3:0] B,
  input  C0,
  output out_4,
  output [4:0] C
);

  wire adder_1_c, adder_2_c, adder_3_c;

  adder adder_1 (.in_1(A[0]), .in_2(B[0]), .in_3(C0), .S(C[0]), .C(adder_1_c));
  adder adder_2 (.in_1(A[1]), .in_2(B[1]), .in_3(adder_1_c), .S(C[1]), .C(adder_2_c));
  adder adder_3 (.in_1(A[2]), .in_2(B[2]), .in_3(adder_2_c), .S(C[2]), .C(adder_3_c));
  adder adder_4 (.in_1(A[3]), .in_2(B[3]), .in_3(adder_3_c), .S(C[3]), .C(C[4]));

  assign out_4 = C[4];
endmodule

module Halte_Lenteng_Lantung (
  input  in_1,
  output [3:0] A
);

  not not_1 (A[3], in_1);
  or or_1 (A[2], A[3], in_1);

  assign A[1:0] = {A[2], in_1};
endmodule

module Halte_Pondok_Jepang (
  input  [1:0] A,
  output [3:0] A_2
);

  wire not_2_out;

  not not_1 (A_2[1], A[0]);
  not not_2 (not_2_out, A[1]);
  and and_1 (A_2[0], A[1], A[0]);
  xnor xnor_1 (A_2[3], A[0], A[1]);
  xor xor_1 (A_2[2], A_2[1], not_2_out);
endmodule

module Multiplexer_Lenteng_Lantung (
  input  in_1,
  input  [3:0] Jalur_0,
  input  [3:0] Jalur_1,
  output [3:0] Penumpang_halte_Lenteng_Lantung
);

  wire not_1_out;
  wire [3:0] and_1_out, and_5_out;

  not not_1 (not_1_out, in_1);
  and and_1 (and_1_out[0], not_1_out, Jalur_0[0]);
  and and_2 (and_1_out[1], not_1_out, Jalur_0[1]);
  and and_3 (and_1_out[2], not_1_out, Jalur_0[2]);
  and and_4 (and_1_out[3], not_1_out, Jalur_0[3]);
  and and_5 (and_5_out[0], Jalur_1[0], in_1);
  and and_6 (and_5_out[1], Jalur_1[1], in_1);
  and and_7 (and_5_out[2], Jalur_1[2], in_1);
  and and_8 (and_5_out[3], Jalur_1[3], in_1);
  assign Penumpang_halte_Lenteng_Lantung = and_1_out | and_5_out;  // OR_Gate or_1, 4 bits wide
endmodule

module Multiplexer_Pondok_Jepang (
  input  in_1,
  input  in_2,
  input  [3:0] Jalur_0,
  input  [3:0] Jalur_1,
  input  [3:0] Jalur_2,
  input  [3:0] Jalur_3,
  output [3:0] Penumpang_halte_Pondok_Jepang
);

  wire not_1_out, not_2_out;
  wire [3:0] and_1_out, and_5_out, and_9_out, and_13_out;

  not not_1 (not_1_out, in_2);
  not not_2 (not_2_out, in_1);
  and and_1 (and_1_out[0], not_2_out, not_1_out, Jalur_0[0]);
  and and_2 (and_1_out[1], not_2_out, not_1_out, Jalur_0[1]);
  and and_3 (and_1_out[2], not_2_out, not_1_out, Jalur_0[2]);
  and and_4 (and_1_out[3], not_2_out, not_1_out, Jalur_0[3]);
  and and_5 (and_5_out[0], Jalur_1[0], not_2_out, in_2);
  and and_6 (and_5_out[1], Jalur_1[1], not_2_out, in_2);
  and and_7 (and_5_out[2], Jalur_1[2], not_2_out, in_2);
  and and_8 (and_5_out[3], Jalur_1[3], not_2_out, in_2);
  and and_9 (and_9_out[0], Jalur_2[0], in_1, not_1_out);
  and and_10 (and_9_out[1], Jalur_2[1], in_1, not_1_out);
  and and_11 (and_9_out[2], Jalur_2[2], in_1, not_1_out);
  and and_12 (and_9_out[3], Jalur_2[3], in_1, not_1_out);
  and and_13 (and_13_out[0], Jalur_3[0], in_1, in_2);
  and and_14 (and_13_out[1], Jalur_3[1], in_1, in_2);
  and and_15 (and_13_out[2], Jalur_3[2], in_1, in_2);
  and and_16 (and_13_out[3], Jalur_3[3], in_1, in_2);
  assign Penumpang_halte_Pondok_Jepang = and_1_out | and_5_out | and_9_out | and_13_out;  // OR_Gate or_1, 4 bits wide
endmodule

module binary_converter_3_bit (
  input  Bit1,
  input  Bit2,
  input  Bit3,
  input  Bit4,
  output O0,
  output O1,
  output O2,
  output O3,
  output O4,
  output O5,
  output O6,
  output O7
);

  wire not_1_out, not_2_out, not_3_out, not_4_out, not_5_out, not_6_out, not_7_out, not_8_out, not_9_out,
       not_10_out, not_11_out, not_12_out, not_13_out, not_14_out, not_15_out, not_16_out, not_17_out,
       not_18_out, not_19_out, not_20_out;

  not not_1 (not_1_out, Bit1);
  not not_2 (not_2_out, Bit2);
  not not_3 (not_3_out, Bit3);
  not not_4 (not_4_out, Bit4);
  not not_5 (not_5_out, Bit1);
  not not_6 (not_6_out, Bit2);
  not not_7 (not_7_out, Bit4);
  not not_8 (not_8_out, Bit1);
  not not_9 (not_9_out, Bit3);
  not not_10 (not_10_out, Bit4);
  not not_11 (not_11_out, Bit1);
  not not_12 (not_12_out, Bit4);
  not not_13 (not_13_out, Bit2);
  not not_14 (not_14_out, Bit3);
  not not_15 (not_15_out, Bit4);
  not not_16 (not_16_out, Bit2);
  not not_17 (not_17_out, Bit4);
  not not_18 (not_18_out, Bit3);
  not not_19 (not_19_out, Bit4);
  not not_20 (not_20_out, Bit4);
  and and_1 (O0, not_1_out, not_2_out, not_3_out, not_4_out);
  and and_2 (O1, not_5_out, not_6_out, Bit3, not_7_out);
  and and_3 (O2, not_8_out, Bit2, not_9_out, not_10_out);
  and and_4 (O3, not_11_out, Bit2, Bit3, not_12_out);
  and and_5 (O4, Bit1, not_13_out, not_14_out, not_15_out);
  and and_6 (O5, Bit1, not_16_out, Bit3, not_17_out);
  and and_7 (O6, Bit1, Bit2, not_18_out, not_19_out);
  and and_8 (O7, Bit1, Bit2, Bit3, not_20_out);
endmodule

module binary_converter_4_bit (
  input  [3:0] Jumlah_penumpang,
  output out_2,
  output out_3,
  output out_4,
  output out_5,
  output out_6,
  output out_7,
  output out_8,
  output out_9,
  output out_10,
  output out_11,
  output out_12,
  output out_13,
  output out_14,
  output out_15,
  output out_16,
  output out_17
);

  wire not_1_out;

  not not_1 (not_1_out, Jumlah_penumpang[3]);
  binary_converter_3_bit binary_converter_3_bit_1 (
    .Bit1(Jumlah_penumpang[2]), .Bit2(Jumlah_penumpang[1]), .Bit3(Jumlah_penumpang[0]),
    .Bit4(Jumlah_penumpang[3]), .O0(out_2), .O1(out_3), .O2(out_4), .O3(out_5), .O4(out_6), .O5(out_7),
    .O6(out_8), .O7(out_9));
  binary_converter_3_bit binary_converter_3_bit_2 (
    .Bit1(Jumlah_penumpang[2]), .Bit2(Jumlah_penumpang[1]), .Bit3(Jumlah_penumpang[0]), .Bit4(not_1_out),
    .O0(out_10), .O1(out_11), .O2(out_12), .O3(out_13), .O4(out_14), .O5(out_15), .O6(out_16), .O7(out_17));
endmodule
