// Logisim project Lab3_TOP_B_ClementSamuelMarly_2206082114.circ as structural Verilog: 3 circuits, main circuit Register
module Register (
  input  [3:0] \input ,
  input  Clock,
  input  Enable,
  output [3:0] out_4
);

  wire not_1_out, not_2_out, not_3_out, not_4_out;

  not not_1 (not_1_out, \input [0]);
  not not_2 (not_2_out, \input [1]);
  not not_3 (not_3_out, \input [2]);
  not not_4 (not_4_out, \input [3]);
  S_R_Flip_Flop s_r_ff_1 (
    .S(\input [0]), .clk(Clock), .R(not_1_out), .Q(out_4[0]), .en(Enable));  // open: Qn, preset, reset
  S_R_Flip_Flop s_r_ff_2 (
    .S(\input [1]), .clk(Clock), .R(not_2_out), .Q(out_4[1]), .en(Enable));  // open: Qn, preset, reset
  S_R_Flip_Flop s_r_ff_3 (
    .S(\input [2]), .clk(Clock), .R(not_3_out), .Q(out_4[2]), .en(Enable));  // open: Qn, preset, reset
  S_R_Flip_Flop s_r_ff_4 (
    .S(\input [3]), .clk(Clock), .R(not_4_out), .Q(out_4[3]), .en(Enable));  // open: Qn, preset, reset
endmodule

module File_Register (
  input  [3:0] Input,
  input  [1:0] Write_Selector,
  input  Clock,
  input  Write_Enable,
  input  [3:0] Monitor___Read_Selector,
  output [3:0] Ahmad,
  output [3:0] Budi
);

  wire and_1_out, decoder_1_out0, decoder_1_out1, decoder_1_out2, decoder_1_out3;
  wire [3:0] register_1_out_4, register_2_out_4, register_3_out_4, register_4_out_4;

  Decoder #(.select(2), .enable("false")) decoder_1 (
    .out0(decoder_1_out0), .out1(decoder_1_out1), .out2(decoder_1_out2), .out3(decoder_1_out3),
    .sel(Write_Selector));
  and and_1 (and_1_out, Clock, Write_Enable);
  Register register_1 (.\input (Input), .Clock(and_1_out), .Enable(decoder_1_out0), .out_4(register_1_out_4));
  Register register_2 (.\input (Input), .Clock(and_1_out), .Enable(decoder_1_out1), .out_4(register_2_out_4));
  Register register_3 (.\input (Input), .Clock(and_1_out), .Enable(decoder_1_out2), .out_4(register_3_out_4));
  Register register_4 (.\input (Input), .Clock(and_1_out), .Enable(decoder_1_out3), .out_4(register_4_out_4));
  Multiplexer #(.select(2), .width(4), .enable("false")) multiplexer_1 (
    .in0(register_1_out_4), .in1(register_2_out_4), .in2(register_3_out_4), .in3(register_4_out_4),
    .out(Ahmad), .sel(Monitor___Read_Selector[1:0]));
  Multiplexer #(.select(2), .width(4), .enable("false")) multiplexer_2 (
    .in0(register_1_out_4), .in1(register_2_out_4), .in2(register_3_out_4), .in3(register_4_out_4),
    .out(Budi), .sel(Monitor___Read_Selector[3:2]));
endmodule

module Main (
  input  [3:0] Input,
  input  [1:0] Write_Selector,
  input  Write_Enable,
  input  [3:0] Read_Selector,
  output [3:0] Monitor_Ahmad,
  output [3:0] Monitor_Budi
);

  wire Clock_out;

  Clock Clock (.out(Clock_out));
  File_Register file_register_1 (
    .Input(Input), .Write_Selector(Write_Selector), .Clock(Write_Enable), .Write_Enable(Clock_out),
    .Ahmad(Monitor_Ahmad), .Budi(Monitor_Budi), .Monitor___Read_Selector(Read_Selector));
endmodule
